// Logisim project My circut1.circ as structural Verilog: 1 circuit, main circuit main
module main (
  input  Cin,
  input  A,
  input  B,
  output Sum,
  output Cout,
  output out_6,
  output out_7
);

  Multiplexer #(.select(2)) multiplexer_1 (
    .in0(A), .in1(B), .in2(B), .in3(A), .out(out_6), .sel({Cin, A}));  // open: en
  Multiplexer #(.select(2)) multiplexer_2 (
    .in0(A), .in1(B), .in2(B), .in3(A), .out(out_7), .sel({Cin, A}));  // open: en
  Adder #(.width(1)) adder_1 (.a(A), .b(B), .out(Sum), .cin(Cin), .cout(Cout));
endmodule
