// Logisim project FullAdder.circ as structural Verilog: 1 circuit, main circuit main
module main (
  input  b,
  input  cin,
  input  a,
  output sum,
  output cout
);

  wire and_1_out, and_2_out, and_3_out, not_1_out;

  not not_1 (not_1_out, b);
  Multiplexer #(.select(2), .enable("false")) multiplexer_1 (
    .in0(b), .in1(not_1_out), .in2(not_1_out), .in3(b), .out(sum), .sel({a, cin}));
  and and_1 (and_1_out, cin, a);
  or or_1 (cout, and_1_out, and_2_out, and_3_out);
  and and_2 (and_2_out, cin, b);
  and and_3 (and_3_out, a, b);
endmodule
