// Logisim project stateMachine.circ as structural Verilog: 1 circuit, main circuit main
module main (
  input  in_1,
  input  in_2,
  output [1:0] out_3,
  output [1:0] out_4
);

  ROM #(.addrWidth(3), .dataWidth(2)) rom_1 (.addr({in_1, out_3}), .data(out_4));  // open: sel
  Clock clock_1 (.out(in_2));
  Register #(.width(2)) register_1 (.D(out_4), .Q(out_3), .clk(in_2));  // open: en, clr

  // Notes on the sheet:
  //   contents of rom_1 (hex, n*v repeats v):
  //   0 0 0 1 1 0 1 1
endmodule
