// Logisim project vend.circ as structural Verilog: 2 circuits, main circuit main
module main (
  input  clock,
  input  reset,
  output [2:0] state
);

  wire Bogus_out, dime_out, nickle_out, quarter_out;
  wire [1:0] priority_encoder_1_out;
  wire [2:0] rom_1_data;

  Button Bogus (.out(Bogus_out));
  Button nickle (.out(nickle_out));
  Button dime (.out(dime_out));
  Button quarter (.out(quarter_out));
  Priority_Encoder #(.select(2)) priority_encoder_1 (
    .in0(Bogus_out), .in1(nickle_out), .in2(dime_out), .in3(quarter_out), .out(priority_encoder_1_out));  // open: gs, en_out, en_in
  // Probe on priority_encoder_1_out
  ROM #(.addrWidth(5), .dataWidth(3)) rom_1 (.addr({state, priority_encoder_1_out}), .data(rom_1_data));  // open: sel
  Clock clock_1 ();  // open: out
  Register #(.width(3)) Register (.D(rom_1_data), .Q(state), .clk(clock), .clr(reset));  // open: en

  // Notes on the sheet:
  //   current state
  //   Next state
  //   contents of rom_1 (hex, n*v repeats v):
  //   0 1 2 5 1 2 3 6 2 3 4 6 3 4 5 6 4 5 7*6 1 2 5
endmodule

module vending_machine (
);

  main main_1 ();  // open: clock, reset, state
endmodule
